# Fritzing sketch 2HeltecWiFiLoRa32V2_communication (saved by Fritzing 0.9.3b)
breadboards: 2

parts:
  Heltec_WiFi_LoRa_32_V3 = Heltec WiFi LoRa 32 V2 [part_number=HTIT-WB32LA]
  ButtonA1 = Pushbutton [package="[THT]"]
  ButtonB1 = Pushbutton [package="[THT]"]
  Heltec_WiFi_LoRa_32_V4 = Heltec WiFi LoRa 32 V2 [part_number=HTIT-WB32LA]
  LED2 = LED - 5mm [color="Red (633nm)" package="5 mm [THT]"]
  R2 = Resistor [tolerance=±5% resistance=220 package=THT]

nets:
  N1: Heltec_WiFi_LoRa_32_V3.pin_16, Heltec_WiFi_LoRa_32_V3.pin_17
  N2: Heltec_WiFi_LoRa_32_V3.pin_18, Heltec_WiFi_LoRa_32_V3.pin_19, ButtonA1.Pin_1, ButtonA1.Pin_2, ButtonB1.Pin_1, ButtonB1.Pin_2
  N3: Heltec_WiFi_LoRa_32_V3.pin_21, Heltec_WiFi_LoRa_32_V3.pin_22
  N4: Heltec_WiFi_LoRa_32_V3.pin_33, ButtonB1.Pin_3, ButtonB1.Pin_4
  N5: Heltec_WiFi_LoRa_32_V3.pin_35, ButtonA1.Pin_3, ButtonA1.Pin_4
  N6: Heltec_WiFi_LoRa_32_V4.pin_16, Heltec_WiFi_LoRa_32_V4.pin_17
  N7: Heltec_WiFi_LoRa_32_V4.pin_18, Heltec_WiFi_LoRa_32_V4.pin_19, R2.Pin_0
  N8: Heltec_WiFi_LoRa_32_V4.pin_21, Heltec_WiFi_LoRa_32_V4.pin_22
  N9: Heltec_WiFi_LoRa_32_V4.pin_35, LED2.cathode
  N10: LED2.anode, R2.Pin_1

notes:
  Transmitter
  Receiver

custom parts:
  Heltec WiFi LoRa 32 V2: Heltec WiFi LoRa 32 V2 WiFi LoRa 32 is a classic IoT dev-board designed & produced by Heltec Automation(TM). It’s a highly integrated product based on ESP32 + SX127x, it has Wi-Fi, BLE, LoRa functions, also Li-Po battery management system, 0.96″ OLED are also included. It’s the best choice for smart cities, smart farms, smart home, and IoT makers.
